// Logisim project hw03.2.12.circ as structural Verilog: 2 circuits, main circuit main
module main (
  input  in_1,
  input  B,
  input  Y,
  input  C
);

  wire nand_1_out, nand_2_out, nand_3_out, nand_4_out;

  nand nand_1 (nand_1_out, in_1, B);
  nand nand_2 (nand_2_out, B, C);
  nand nand_3 (nand_3_out, in_1, C);
  nand nand_4 (nand_4_out, nand_1_out, nand_2_out, nand_3_out);

  // Notes on the sheet:
  //   A
endmodule

module mm (
  input  A,
  input  B,
  input  _1,
  input  Y,
  input  C
);

  wire nand_1_out, nand_2_out, nand_3_out, nand_4_out, nand_5_out, not_1_out, not_2_out, not_3_out;

  not not_1 (not_1_out, A);
  not not_2 (not_2_out, B);
  not not_3 (not_3_out, C);
  nand nand_1 (nand_1_out, A, B, not_3_out);
  nand nand_2 (nand_2_out, A, not_2_out, C);
  nand nand_3 (nand_3_out, C, not_1_out, B);
  nand nand_4 (nand_4_out, nand_1_out, nand_2_out, nand_3_out);
  nand nand_5 (nand_5_out, nand_4_out, _1);
endmodule
