// Logisim project hw03.2.13.circ as structural Verilog: 2 circuits, main circuit main
module main (
  input  in_1,
  input  B,
  input  Y,
  input  C
);

  wire nor_1_out, nor_2_out, nor_3_out, nor_4_out, not_1_out, not_2_out, not_3_out;

  not not_1 (not_1_out, in_1);
  not not_2 (not_2_out, B);
  not not_3 (not_3_out, C);
  nor nor_1 (nor_1_out, in_1, C);
  nor nor_2 (nor_2_out, not_1_out, B, not_3_out);
  nor nor_3 (nor_3_out, not_1_out, not_2_out, not_3_out);
  nor nor_4 (nor_4_out, nor_1_out, nor_2_out, nor_3_out);

  // Notes on the sheet:
  //   A
endmodule

module mm (
  input  in_1,
  input  B,
  input  in_3,
  input  C,
  input  in_5,
  input  in_6
);

  wire nor_1_out, nor_2_out, nor_3_out, nor_4_out, nor_5_out, nor_6_out, not_1_out, not_2_out, not_3_out,
       not_4_out;

  not not_1 (not_1_out, in_1);
  not not_2 (not_2_out, B);
  not not_3 (not_3_out, C);
  not not_4 (not_4_out, in_5);
  nor nor_1 (nor_1_out, not_1_out, not_2_out, C);
  nor nor_2 (nor_2_out, B, not_3_out);
  nor nor_3 (nor_3_out, nor_1_out, nor_2_out, in_5);
  nor nor_4 (nor_4_out, in_1, B, not_4_out);
  nor nor_5 (nor_5_out, nor_3_out, nor_4_out);
  nor nor_6 (nor_6_out, nor_5_out, in_6);

  // Notes on the sheet:
  //   A
  //   D
  //   0
  //   Y
endmodule
